# Fritzing sketch SchemaFritzing (saved by Fritzing 0.9.3b)
breadboards: 1

parts:
  Componente1 = Arduino Uno (Rev3)
  LED1 = LED - 5mm [color="Green (570nm)" package="5 mm [THT]"]
  LED2 = LED - 5mm [color="Green (570nm)" package="5 mm [THT]"]
  LED3 = LED - 5mm [color="Green (570nm)" package="5 mm [THT]"]
  LED4 = LED - 5mm [color="White (4500K)" package="5 mm [THT]"]
  LED5 = LED - 5mm [color="Red (633nm)" package="5 mm [THT]"]
  R2 = Resistor [tolerance=±5% resistance=220 package=THT]
  R3 = Resistor [tolerance=±5% resistance=220 package=THT]
  R4 = Resistor [tolerance=±5% resistance=220 package=THT]
  R5 = Resistor [tolerance=±5% resistance=220 package=THT]
  R6 = Resistor [tolerance=±5% resistance=220 package=THT]
  S2 = Pushbutton [package="[THT]"]
  R8 = Resistor [tolerance=±5% resistance=10k package=THT]
  S3 = Pushbutton [package="[THT]"]
  R10 = Rotary Potentiometer (Small) [maximum_resistance=100kΩ package=THT]
  R11 = Resistor [tolerance=±5% resistance=10k package=THT]

nets:
  N1: Componente1.A0, R10.wiper
  N2: Componente1.D8, R3.Pin_0
  N3: Componente1.D12/MISO, R2.Pin_0
  N4: Componente1.D13/SCK, R4.Pin_0
  N5: Componente1.GND, LED1.anode, LED2.anode, LED3.anode, LED4.anode, LED5.anode, R8.Pin_0, R10.leg2, R11.Pin_1
  N6: Componente1.D2, S2.Pin_1, S2.Pin_2, R8.Pin_1
  N7: Componente1.D3_PWM, S3.Pin_1, S3.Pin_2, R11.Pin_0
  N8: Componente1.D4, R6.Pin_0
  N9: Componente1.D6_PWM, R5.Pin_0
  N10: Componente1.5V, S2.Pin_3, S2.Pin_4, S3.Pin_3, S3.Pin_4, R10.leg1
  N11: LED1.cathode, R4.Pin_1
  N12: LED2.cathode, R2.Pin_1
  N13: LED3.cathode, R3.Pin_1
  N14: LED4.cathode, R5.Pin_1
  N15: LED5.cathode, R6.Pin_1
