# Fritzing sketch sd-edge (saved by Fritzing 0.9.3b)
breadboards: 1

parts:
  ESP8267 = NodeMCU V1.0
  LED2 = LED - 5mm [color="Red (633nm)" package="5 mm [THT]"]
  R1 = Resistor [tolerance=±5% resistance=220 package=THT]
  LED3 = smd LED [color="Red (633nm)" package="0603 [SMD]"]
  LED3_2 = smd LED [color="Green (570nm)" package="0805 [SMD]"]
  R2 = Resistor [tolerance=±5% resistance=220 package=THT]
  R3 = Rotary Potentiometer (Small) [maximum_resistance=100kΩ package=THT]

nets:
  N1: ESP8267.D1, R1.Pin_0
  N2: ESP8267.D2, R2.Pin_0
  N3: ESP8267.3V3, R3.leg2
  N4: ESP8267.GND, LED2.cathode, LED3.cathode, LED3_2.cathode, R3.leg1
  N5: ESP8267.A0, R3.wiper
  N6: LED2.anode, R2.Pin_1
  N7: R1.Pin_1, LED3.anode, LED3_2.anode

custom parts:
  NodeMCU V1.0: ESP8266 based NodeMCU
